// Digital circuit display.dig as structural Verilog
module display (
  input  clock,
  input  enable,
  input  [15:0] Character_Data,
  output [3:0] R,
  output [3:0] G,
  output [3:0] B,
  output H_output,
  output V_output,
  output [10:0] Character_Address
);

  wire vga_char_position_1_p5, vga_char_position_1_p6, vga_sync_1_horizontal, vga_sync_1_picture,
       vga_sync_1_vertical;
  wire [3:0] vga_char_position_1_p4;
  wire [4:0] vga_char_position_1_p3;
  wire [6:0] vga_words_1_p27;
  wire [11:0] vga_words_1_p28, vga_words_1_p29;
  wire [15:0] vga_sync_1_x, vga_sync_1_y;

  vga_sync vga_sync_1 (
    .clock(clock), .Horizontal(vga_sync_1_horizontal), .Vertical(vga_sync_1_vertical),
    .picture(vga_sync_1_picture), .X(vga_sync_1_x), .Y(vga_sync_1_y));
  // vga_Char_position vga_char_position_1: pin names not known; wires that end beside it: vga_sync_1_x, vga_sync_1_y, vga_char_position_1_p3, vga_char_position_1_p4, vga_char_position_1_p5, vga_char_position_1_p6
  // VGA_words vga_words_1: pin names not known; wires that end beside it: vga_char_position_1_p5, vga_char_position_1_p6, 12'h9e, 12'h1, {7{1'b0}}, 12'h3c1, 12'h1, 4'b0010, {8{1'b0}}, 7'b0111000, 7'b0101101, 7'b1000010, 7'b1010101, 7'b1010100, 7'b0100000, 7'b1001101, 7'b1001001, 7'b1000111, 7'b1001000, 7'b1010100, 7'b1011001, 7'b0100000, 7'b1010110, 7'b1000111, 7'b1000001, enable, vga_words_1_p27, vga_words_1_p28, vga_words_1_p29
  vga_text vga_text_1 (
    .H_input(vga_sync_1_horizontal), .V_input(vga_sync_1_vertical), .picture(vga_sync_1_picture),
    .row(vga_char_position_1_p3), .column(vga_char_position_1_p4), .clock(clock),
    .character(vga_words_1_p27), .foreground(vga_words_1_p28), .background(vga_words_1_p29),
    .Character_Data(Character_Data), .R(R), .G(G), .B(B), .H_output(H_output), .V_output(V_output),
    .Character_Address(Character_Address));

  // Other names for the same wires on the sheet: C = clock

  // Notes on the sheet:
  //   clock: Hz: 2147483647
endmodule
